# Fritzing sketch space_invaders (saved by Fritzing 0.9.4)
breadboards: 2

parts:
  Part1 = Arduino Uno (Rev3) - ICSP
  Raspberry_Pi_1 = Raspberry Pi 3 [part_number=RPI-3-V1.2]
  LED1 = LED - 5mm [color="Red (633nm)" package="5 mm [THT]"]
  LED2 = LED - 5mm [color="Red (633nm)" package="5 mm [THT]"]
  LED3 = LED - 5mm [color="Red (633nm)" package="5 mm [THT]"]
  LED4 = LED - 5mm [color="Red (633nm)" package="5 mm [THT]"]
  LED5 = LED - 5mm [color="Red (633nm)" package="5 mm [THT]"]
  Part3 = LCD1602-I2C
  Part4 = Thumb Joystick
  R1 = Resistor [tolerance=±5% resistance=330 package="0805 [SMD]"]
  R2 = Resistor [tolerance=±5% resistance=330 package="0805 [SMD]"]
  R3 = Resistor [tolerance=±5% resistance=330 package="0805 [SMD]"]
  R4 = Resistor [tolerance=±5% resistance=330 package="0805 [SMD]"]
  R5 = Resistor [tolerance=±5% resistance=330 package="0805 [SMD]"]
  S6 = Pushbutton [package="[THT]"]
  S7 = Pushbutton [package="[THT]"]

nets:
  N1: Part1.A1, Part4.HORZ
  N2: Part1.A2, Part4.VERT
  N3: Part1.D2, S6.Pin_1, S6.Pin_2
  N4: Part1.D3_PWM, S7.Pin_1, S7.Pin_2
  N5: Part1.D6_PWM, Part4.SEL
  5V: Part1.5V, Part4.VCC
  GND: Part1.GND, Part4.GND
  N6: Raspberry_Pi_1.3v3, Raspberry_Pi_1.GPIO2, Part3.SDA
  N7: Raspberry_Pi_1.GPIO3, Part3.SCL
  N8: Raspberry_Pi_1.GPIO5, R5.Pin_1
  N9: Raspberry_Pi_1.GPIO6, R4.Pin_1
  N10: Raspberry_Pi_1.GPIO13, R3.Pin_1
  N11: Raspberry_Pi_1.GPIO19, R2.Pin_1
  N12: Raspberry_Pi_1.GPIO26, R1.Pin_1
  GND_2: Raspberry_Pi_1.GND, LED1.cathode, LED2.cathode, LED3.cathode, LED4.cathode, LED5.cathode, Part3.GND
  5V_2: Raspberry_Pi_1.5V, Part3.VCC
  N13: LED1.anode, R1.Pin_0
  N14: LED2.anode, R2.Pin_0
  N15: LED3.anode, R4.Pin_0
  N16: LED4.anode, R5.Pin_0
  N17: LED5.anode, R3.Pin_0
  N18: S6.Pin_3, S6.Pin_4, S7.Pin_3, S7.Pin_4

custom parts:
  LCD1602-I2C: A standard character display, usually with 2x16 characters. Comes in many colors with LCM1602 IIC attached.
